# Fritzing sketch hassbeam (saved by Fritzing 1.0.2b)
circuit board: 4cm x 6cm
perfboards: 1

parts:
  D1 = LTE-302 [package=lte-302]
  U1 = ESP32S-HiLetgo [part_number=ESP32]
  R1 = Resistor [tolerance=±5% resistance=11 package="0805 [SMD]"]
  R2 = Resistor [tolerance=±5% resistance=1k package="0805 [SMD]"]
  IR = TSOP4838 [form="♀ (female)" package=THT]
  R3 = Resistor [tolerance=±5% resistance=100 package="0805 [SMD]"]
  J1 = Power Header [form="♀ (female)" package=THT]
  Q1 = NPN-Transistor [package="TO92 [THT]"]
  C1 = Ceramic Capacitor [capacitance=100nF voltage=35V package="100 mil [THT, multilayer]"]

nets:
  N1: D1.A, R1.Pin_1
  N2: D1.C, Q1.C
  N3: U1.3.3, R1.Pin_0, R3.Pin_1, J1.3.3v
  N4: U1.GPIO27, R2.Pin_1
  N5: U1.GPIO14, IR.OUT
  GND: U1.GND, IR.GND, J1.GND, Q1.E, C1.1
  VIN: U1.VIN, J1.5v
  N6: R2.Pin_0, Q1.B
  N7: IR.VCC, R3.Pin_0, C1.0

custom parts:
  ESP32S-HiLetgo: HiLetgo ESP-WROOM-32 ESP32 ESP-32S Development Board 2.4GHz Dual-Mode WiFi + Bluetooth Dual Cores Microcontroller The ESP32 integrated with Antenna switches, RF Balun, power amplifiers, low-noise amplifiers, filters, and management modules, and the entire solution occupies the least area of PCB. 2.4 GHz Wi-Fi plus Bluetooth dual-mode chip, with TSMC Ultra-low power consumption 40nm technology,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
  TSOP4838: TSOP4838 IR receiver
  Power Header: Generic female header
