# Fritzing sketch universal remote (saved by Fritzing 1.0.2b)
circuit board: 3.50121cm x 5cm
perfboards: 1

parts:
  Q1 = NPN-Transistor [package="TO92 [THT]"]
  D1 = LTE-302 [package=lte-302]
  R1 = Resistor [tolerance=±5% resistance=22 package="0402 [SMD]"]
  R2 = Resistor [tolerance=±5% resistance=22 package="0402 [SMD]"]
  U1 = ESP32S-HiLetgo [part_number=ESP32]
  power = Generic female header - 2 pins [form="♀ (female)" package=THT]
  J1 = Generic female header - 3 pins [form="♀ (female)" package=THT]

nets:
  GND: Q1.E, U1.GND, power.GND, J1.GND
  N1: Q1.B, D1.C
  N2: Q1.C, U1.GPIO27
  N3: D1.A, R1.Pin_0, R1.Pin_1, R2.Pin_0, R2.Pin_1, U1.3.3, J1.VCC
  N4: U1.GPIO14, J1.OUT
  VIN: U1.VIN, power.VCC

custom parts:
  ESP32S-HiLetgo: HiLetgo ESP-WROOM-32 ESP32 ESP-32S Development Board 2.4GHz Dual-Mode WiFi + Bluetooth Dual Cores Microcontroller The ESP32 integrated with Antenna switches, RF Balun, power amplifiers, low-noise amplifiers, filters, and management modules, and the entire solution occupies the least area of PCB. 2.4 GHz Wi-Fi plus Bluetooth dual-mode chip, with TSMC Ultra-low power consumption 40nm technology,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
  Generic female header - 2 pins: Generic female header
  Generic female header - 3 pins: Generic female header
